# Fritzing sketch Barramento_EITduino (saved by Fritzing 0.9.6b)
breadboards: 1

parts:
  Sinais = female pin header, 27 pins [form="♀ (female)"]
  Comunicacao = female pin header, 35 pins [form="♀ (female)"]
  tensoes = female pin header, 8 pins [form="♀ (female)"]  # not connected

nets:
  I1: Sinais.pin20
  I2: Sinais.pin21
  AmpI1: Sinais.pin22
  AmpI2: Sinais.pin23
  Sin1: Sinais.pin24
  Sin2: Sinais.pin25
  SinA: Sinais.pin26
  SinB: Sinais.pin27
  SINC: Comunicacao.pin1
  SPI_SIMO: Comunicacao.pin2
  SPI_MISO: Comunicacao.pin3
  SPI_clk: Comunicacao.pin4
  CS (AD9833): Comunicacao.pin5
  SCL_3: Comunicacao.pin30
  SDA_3: Comunicacao.pin31
  SCL_2: Comunicacao.pin32
  SDA_2: Comunicacao.pin33
  SCL_1: Comunicacao.pin34
  SDA_1: Comunicacao.pin35

notes:
  -12V
  +9V
  -9V
  +5V
  -5V
  3.3V
  GND
  +12V
  SinB
  SinA
  Sin2
  Sin1
  AmpI2
  AmpI1
  I2
  I1
  SINC
  SPI_SIMO
  SPI_MISO
  SPI_clk
  CS(AD9833)
  SDA1
  SCL1
  SDA2
  SCL2
  SDA3
  SCL3
  CS(x9c10x)
